// Logisim project control_logic.circ as structural Verilog: 1 circuit, main circuit control_logic
module control_logic (
  input  [31:0] inst,
  input  BrEq,
  input  BrLt,
  output PCSel,
  output RegWEn,
  output [2:0] ImmSel,
  output BrUn,
  output ASel,
  output BSel,
  output [3:0] ALUSel,
  output MemRW,
  output [1:0] WBSel,
  output CSRSel,
  output CSRWen
);

  wire and1, and_2_out, and_3_out, and_4_out, and_5_out, and_6_out, and_7_out, and_8_out, and_9_out,
       and_10_out, and_11_out, and_12_out, and_13_out, and_15_out, comparator_2_eq, comparator_3_eq,
       comparator_4_eq, comparator_5_eq, comparator_7_eq, comparator_8_eq, comparator_9_eq, comparator_10_eq,
       comparator_12_eq, comparator_13_eq, comparator_14_eq, comparator_15_eq, comparator_16_eq,
       comparator_17_eq, comparator_18_eq, comparator_19_eq, comparator_20_eq, comparator_21_eq,
       comparator_22_eq, comparator_23_eq, comparator_24_eq, comparator_25_eq, comparator_26_eq,
       comparator_27_eq, comparator_28_eq, comparator_29_eq, comparator_34_eq, comparator_35_eq,
       comparator_36_eq, comparator_37_eq, comparator_38_eq, comparator_39_eq, comparator_40_eq,
       comparator_41_eq, comparator_43_eq, comparator_44_eq, comparator_45_eq, comparator_46_eq,
       comparator_47_eq, comparator_48_eq, comparator_49_eq, comparator_50_eq, comparator_51_eq,
       comparator_52_eq, mul10, mulh14, mulhu11, not_1_out, not_2_out, not_3_out, not_4_out, not_5_out, or2,
       or_1_out, or_2_out, or_12_out, or_13_out, or_14_out, or_15_out, or_16_out, or_17_out, or_18_out,
       or_19_out, or_20_out, or_21_out, or_22_out, or_23_out, or_24_out, or_25_out, or_26_out, or_27_out,
       or_28_out, or_33_out, or_34_out, or_37_out, or_38_out, or_39_out, or_40_out, or_41_out, sll6, slt7,
       sra5, srl4, sub12, xor3;

  Comparator #(.mode("unsigned"), .width(7)) comparator_1 (.a(inst[6:0]), .b(7'b0100011), .eq(MemRW));  // open: gt, lt
  Comparator #(.mode("unsigned"), .width(7)) comparator_2 (
    .a(inst[6:0]), .b(7'b0100011), .eq(comparator_2_eq));  // open: gt, lt
  Comparator #(.mode("unsigned"), .width(7)) comparator_3 (
    .a(inst[6:0]), .b(7'b1100011), .eq(comparator_3_eq));  // open: gt, lt
  Comparator #(.mode("unsigned"), .width(7)) comparator_4 (
    .a(inst[6:0]), .b(7'b1101111), .eq(comparator_4_eq));  // open: gt, lt
  Comparator #(.mode("unsigned"), .width(7)) comparator_5 (
    .a(inst[6:0]), .b(7'b1100111), .eq(comparator_5_eq));  // open: gt, lt
  Comparator #(.mode("unsigned"), .width(7)) comparator_6 (
    .a(inst[6:0]), .b(7'b0000011), .eq(WBSel[1]));  // open: gt, lt
  Comparator #(.mode("unsigned"), .width(7)) comparator_7 (
    .a(inst[6:0]), .b(7'b0010111), .eq(comparator_7_eq));  // open: gt, lt
  Comparator #(.mode("unsigned"), .width(7)) comparator_8 (
    .a(inst[6:0]), .b(7'b0110111), .eq(comparator_8_eq));  // open: gt, lt
  nor nor_1 (RegWEn, comparator_2_eq, comparator_3_eq);
  or or_1 (or_1_out, comparator_4_eq, comparator_5_eq);
  Comparator #(.mode("unsigned"), .width(7)) comparator_9 (
    .a(inst[6:0]), .b(7'b0100011), .eq(comparator_9_eq));  // open: gt, lt
  or or_2 (or_2_out, comparator_7_eq, comparator_8_eq);
  Comparator #(.mode("unsigned"), .width(7)) comparator_10 (
    .a(inst[6:0]), .b(7'b1100011), .eq(comparator_10_eq));  // open: gt, lt
  Comparator #(.mode("unsigned"), .width(7)) comparator_11 (
    .a(inst[6:0]), .b(7'b1101111), .eq(ImmSel[2]));  // open: gt, lt
  not not_1 (not_1_out, or_1_out);
  not not_2 (not_2_out, WBSel[1]);
  or or_3 (ImmSel[0], comparator_9_eq, or_2_out);
  or or_4 (ImmSel[1], or_2_out, comparator_10_eq);
  and and_1 (WBSel[0], not_1_out, not_2_out);
  Comparator #(.mode("unsigned"), .width(17)) comparator_12 (
    .a({inst[31:25], inst[14:12], inst[6:0]}), .b(17'h3b3), .eq(comparator_12_eq));  // open: gt, lt
  Comparator #(.mode("unsigned"), .width(7)) comparator_13 (
    .a(inst[6:0]), .b(7'b0010011), .eq(comparator_13_eq));  // open: gt, lt
  Comparator #(.mode("unsigned"), .width(3)) comparator_14 (
    .a(inst[14:12]), .b(3'b111), .eq(comparator_14_eq));  // open: gt, lt
  Comparator #(.mode("unsigned"), .width(17)) comparator_15 (
    .a({inst[31:25], inst[14:12], inst[6:0]}), .b(17'h333), .eq(comparator_15_eq));  // open: gt, lt
  Comparator #(.mode("unsigned"), .width(7)) comparator_16 (
    .a(inst[6:0]), .b(7'b0010011), .eq(comparator_16_eq));  // open: gt, lt
  Comparator #(.mode("unsigned"), .width(3)) comparator_17 (
    .a(inst[14:12]), .b(3'b110), .eq(comparator_17_eq));  // open: gt, lt
  Comparator #(.mode("unsigned"), .width(17)) comparator_18 (
    .a({inst[31:25], inst[14:12], inst[6:0]}), .b(17'h233), .eq(comparator_18_eq));  // open: gt, lt
  Comparator #(.mode("unsigned"), .width(7)) comparator_19 (
    .a(inst[6:0]), .b(7'b0010011), .eq(comparator_19_eq));  // open: gt, lt
  Comparator #(.mode("unsigned"), .width(3)) comparator_20 (
    .a(inst[14:12]), .b(3'b100), .eq(comparator_20_eq));  // open: gt, lt
  Comparator #(.mode("unsigned"), .width(17)) comparator_21 (
    .a({inst[31:25], inst[14:12], inst[6:0]}), .b(17'h2b3), .eq(comparator_21_eq));  // open: gt, lt
  Comparator #(.mode("unsigned"), .width(17)) comparator_22 (
    .a({inst[31:25], inst[14:12], inst[6:0]}), .b(17'h293), .eq(comparator_22_eq));  // open: gt, lt
  Comparator #(.mode("unsigned"), .width(17)) comparator_23 (
    .a({inst[31:25], inst[14:12], inst[6:0]}), .b(17'h82b3), .eq(comparator_23_eq));  // open: gt, lt
  Comparator #(.mode("unsigned"), .width(17)) comparator_24 (
    .a({inst[31:25], inst[14:12], inst[6:0]}), .b(17'h8293), .eq(comparator_24_eq));  // open: gt, lt
  Comparator #(.mode("unsigned"), .width(17)) comparator_25 (
    .a({inst[31:25], inst[14:12], inst[6:0]}), .b(17'hb3), .eq(comparator_25_eq));  // open: gt, lt
  Comparator #(.mode("unsigned"), .width(17)) comparator_26 (
    .a({inst[31:25], inst[14:12], inst[6:0]}), .b(17'h93), .eq(comparator_26_eq));  // open: gt, lt
  Comparator #(.mode("unsigned"), .width(17)) comparator_27 (
    .a({inst[31:25], inst[14:12], inst[6:0]}), .b(17'h133), .eq(comparator_27_eq));  // open: gt, lt
  Comparator #(.mode("unsigned"), .width(7)) comparator_28 (
    .a(inst[6:0]), .b(7'b0010011), .eq(comparator_28_eq));  // open: gt, lt
  Comparator #(.mode("unsigned"), .width(3)) comparator_29 (
    .a(inst[14:12]), .b(3'b010), .eq(comparator_29_eq));  // open: gt, lt
  Comparator #(.mode("unsigned"), .width(17)) comparator_30 (
    .a({inst[31:25], inst[14:12], inst[6:0]}), .b(17'h433), .eq(mul10));  // open: gt, lt
  Comparator #(.mode("unsigned"), .width(17)) comparator_31 (
    .a({inst[31:25], inst[14:12], inst[6:0]}), .b(17'h5b3), .eq(mulhu11));  // open: gt, lt
  Comparator #(.mode("unsigned"), .width(17)) comparator_32 (
    .a({inst[31:25], inst[14:12], inst[6:0]}), .b(17'h833), .eq(sub12));  // open: gt, lt
  Comparator #(.mode("unsigned"), .width(17)) comparator_33 (
    .a({inst[31:25], inst[14:12], inst[6:0]}), .b(17'h4b3), .eq(mulh14));  // open: gt, lt
  and and_2 (and_2_out, comparator_13_eq, comparator_14_eq);
  and and_3 (and_3_out, comparator_16_eq, comparator_17_eq);
  and and_4 (and_4_out, comparator_19_eq, comparator_20_eq);
  or or_5 (srl4, comparator_21_eq, comparator_22_eq);
  or or_6 (sra5, comparator_23_eq, comparator_24_eq);
  or or_7 (sll6, comparator_25_eq, comparator_26_eq);
  and and_5 (and_5_out, comparator_28_eq, comparator_29_eq);
  or or_8 (and1, comparator_12_eq, and_2_out);
  or or_9 (or2, comparator_15_eq, and_3_out);
  or or_10 (xor3, comparator_18_eq, and_4_out);
  or or_11 (slt7, comparator_27_eq, and_5_out);
  or or_12 (or_12_out, and1, xor3);
  or or_13 (or_13_out, sra5, slt7);
  or or_14 (or_14_out, mulhu11, 1'b0);
  or or_15 (or_15_out, or2, xor3);
  or or_16 (or_16_out, sll6, slt7);
  or or_17 (or_17_out, mulhu11, mulh14);
  or or_18 (or_18_out, srl4, sra5);
  or or_19 (or_19_out, sll6, slt7);
  or or_20 (or_20_out, 1'b0, mulh14);
  or or_21 (or_21_out, mul10, mulhu11);
  or or_22 (or_22_out, 1'b0, mulh14);
  or or_23 (or_23_out, or_15_out, or_16_out);
  or or_24 (or_24_out, mul10, or_17_out);
  or or_25 (or_25_out, or_18_out, or_19_out);
  or or_26 (or_26_out, sub12, or_20_out);
  or or_27 (or_27_out, or_21_out, sub12);
  or or_28 (or_28_out, or_12_out, or_13_out);
  or or_29 (ALUSel[3], or_27_out, or_22_out);
  or or_30 (ALUSel[0], or_28_out, or_14_out);
  or or_31 (ALUSel[1], or_23_out, or_24_out);
  or or_32 (ALUSel[2], or_25_out, or_26_out);
  Comparator #(.mode("unsigned"), .width(7)) comparator_34 (
    .a(inst[6:0]), .b(7'b1100011), .eq(comparator_34_eq));  // open: gt, lt
  Comparator #(.mode("unsigned"), .width(7)) comparator_35 (
    .a(inst[6:0]), .b(7'b0010111), .eq(comparator_35_eq));  // open: gt, lt
  Comparator #(.mode("unsigned"), .width(7)) comparator_36 (
    .a(inst[6:0]), .b(7'b1101111), .eq(comparator_36_eq));  // open: gt, lt
  Comparator #(.mode("unsigned"), .width(7)) comparator_37 (
    .a(inst[6:0]), .b(7'b0110011), .eq(comparator_37_eq));  // open: gt, lt
  Comparator #(.mode("unsigned"), .width(7)) comparator_38 (
    .a(inst[6:0]), .b(7'b1100011), .eq(comparator_38_eq));  // open: gt, lt
  Comparator #(.mode("unsigned"), .width(3)) comparator_39 (
    .a(inst[14:12]), .b(3'b110), .eq(comparator_39_eq));  // open: gt, lt
  Comparator #(.mode("unsigned"), .width(7)) comparator_40 (
    .a(inst[6:0]), .b(7'b1100011), .eq(comparator_40_eq));  // open: gt, lt
  Comparator #(.mode("unsigned"), .width(3)) comparator_41 (
    .a(inst[14:12]), .b(3'b111), .eq(comparator_41_eq));  // open: gt, lt
  Comparator #(.mode("unsigned"), .width(7)) comparator_42 (
    .a(inst[6:0]), .b(7'b1110011), .eq(CSRWen));  // open: gt, lt
  Comparator #(.mode("unsigned"), .width(3)) comparator_43 (
    .a(inst[14:12]), .b(3'b101), .eq(comparator_43_eq));  // open: gt, lt
  Comparator #(.mode("unsigned"), .width(7)) comparator_44 (
    .a(inst[6:0]), .b(7'b1100111), .eq(comparator_44_eq));  // open: gt, lt
  Comparator #(.mode("unsigned"), .width(7)) comparator_45 (
    .a(inst[6:0]), .b(7'b1101111), .eq(comparator_45_eq));  // open: gt, lt
  Comparator #(.mode("unsigned"), .width(3)) comparator_46 (
    .a(inst[14:12]), .b(3'b000), .eq(comparator_46_eq));  // open: gt, lt
  Comparator #(.mode("unsigned"), .width(3)) comparator_47 (
    .a(inst[14:12]), .b(3'b001), .eq(comparator_47_eq));  // open: gt, lt
  not not_3 (not_3_out, BrEq);
  Comparator #(.mode("unsigned"), .width(3)) comparator_48 (
    .a(inst[14:12]), .b(3'b100), .eq(comparator_48_eq));  // open: gt, lt
  Comparator #(.mode("unsigned"), .width(3)) comparator_49 (
    .a(inst[14:12]), .b(3'b110), .eq(comparator_49_eq));  // open: gt, lt
  Comparator #(.mode("unsigned"), .width(3)) comparator_50 (
    .a(inst[14:12]), .b(3'b101), .eq(comparator_50_eq));  // open: gt, lt
  not not_4 (not_4_out, BrLt);
  Comparator #(.mode("unsigned"), .width(3)) comparator_51 (
    .a(inst[14:12]), .b(3'b111), .eq(comparator_51_eq));  // open: gt, lt
  not not_5 (not_5_out, BrLt);
  or or_33 (or_33_out, comparator_34_eq, comparator_35_eq);
  not not_6 (BSel, comparator_37_eq);
  and and_6 (and_6_out, comparator_38_eq, comparator_39_eq);
  and and_7 (and_7_out, comparator_40_eq, comparator_41_eq);
  or or_34 (or_34_out, comparator_44_eq, comparator_45_eq);
  Comparator #(.mode("unsigned"), .width(7)) comparator_52 (
    .a(inst[6:0]), .b(7'b1100011), .eq(comparator_52_eq));  // open: gt, lt
  and and_8 (and_8_out, comparator_46_eq, BrEq);
  and and_9 (and_9_out, comparator_47_eq, not_3_out);
  and and_10 (and_10_out, comparator_48_eq, BrLt);
  and and_11 (and_11_out, comparator_49_eq, BrLt);
  and and_12 (and_12_out, comparator_50_eq, not_4_out);
  and and_13 (and_13_out, comparator_51_eq, not_5_out);
  or or_35 (ASel, or_33_out, comparator_36_eq);
  or or_36 (BrUn, and_6_out, and_7_out);
  and and_14 (CSRSel, CSRWen, comparator_43_eq);
  or or_37 (or_37_out, and_8_out, and_9_out);
  or or_38 (or_38_out, and_10_out, and_11_out);
  or or_39 (or_39_out, and_12_out, and_13_out);
  or or_40 (or_40_out, or_38_out, or_39_out);
  or or_41 (or_41_out, or_37_out, or_40_out);
  and and_15 (and_15_out, comparator_52_eq, or_41_out);
  or or_42 (PCSel, or_34_out, and_15_out);

  // Other names for the same wires on the sheet: aluop[16:0] = {inst[31:25], inst[14:12], inst[6:0]};
  //   opcode[6:0] = inst[6:0]; func3[2:0] = inst[14:12]; func7[6:0] = inst[31:25]; ALUSel_bit0 = ALUSel[0];
  //   ALUSel_bit1 = ALUSel[1]; ALUSel_bit2 = ALUSel[2]; ALUSel_bit3 = ALUSel[3]; ImmSel_bit0 = ImmSel[0];
  //   ImmSel_bit1 = ImmSel[1]; ImmSel_bit2 = ImmSel[2]; WBSel_bit0 = WBSel[0]; WBSel_bit1 = WBSel[1]

  // Notes on the sheet:
  //   INPUTS to your circuit
  //   DON'T CHANGE THE LOCATIONS OF THE INPUTS AND OUTPUTS!
  //   OUTPUT from your circuit
  //   Truth Table
  //   PC+4                      ALU                         MEM                      WBSel1                       WBSel0
  //   1                             0                             0                                0                                0
  //   0                             1                             0                                0                                1
  //   0                             0                             1                                1                                0
  //   WBSel0 = ALU,  WBSEL1 = MEM
  //   Truth Table
  //   I         S         B         U         J         bit2         bit1         bit0
  //   1         0         0         0         0           0             0             0
  //   0         1         0         0         0           0             0             1
  //   0         0         1         0         0           0             1             0
  //   0         0         0         1         0           0             1             1
  //   0         0         0         0         1           1             0             0
  //   ImmSel0 = S + U,  ImmSel1 = B + U,  ImmSel2 = J
endmodule
