// Logisim project my_cpu_5_stage.circ as structural Verilog: 1 circuit, main circuit cpu
module cpu (
  input  clk,
  input  [31:0] INSTRUCTION,
  input  [31:0] READ_DATA,
  output [31:0] WRITE_ADDRESS,
  output [31:0] PROGRAM_COUNTER,
  output [31:0] ra,
  output [31:0] sp,
  output [31:0] t0,
  output [31:0] t1,
  output [31:0] t2,
  output [31:0] s0,
  output [31:0] s1,
  output [31:0] a0,
  output [31:0] tohost,
  output [3:0] WRITE_ENABLE,
  output [31:0] WRITE_DATA
);

  wire and_1_out, and_2_out, ASel, ASel_EX, BrEq, BrLt, BrUn, BrUn_EX, BSel, BSel_EX, comparator_1_eq,
       comparator_2_eq, comparator_3_eq, comparator_6_eq, comparator_7_eq, comparator_8_eq, comparator_9_eq,
       CSRSel, CSRSel_EX, CSRWen, CSRWen_EX, HAZARD, MemRW, MemRW_EX, MemRW_MEM, not_1_out, not_2_out,
       not_3_out, not_4_out, not_5_out, not_6_out, not_7_out, or_1_out, PCSel, PCSel_EX, RegWEn, RegWEn_EX,
       RegWEn_MEM, RegWEn_WB;
  wire [1:0] FowardingA, FowardingB, WBSel, WBSel_EX, WBSel_MEM, WBSel_WB;
  wire [2:0] ImmSel;
  wire [3:0] ALUSel, ALUSel_EX;
  wire [4:0] rd_field_EX, rd_field_MEM, rd_field_WB, rs1_field_EX, rs2_field_EX;
  wire [11:0] bit_extender_1_out;
  wire [31:0] adder_1_out, ALU_RESULT, ALU_RESULT_WB, CSR_DATA, csr_uimm, imm, imm_EX, INST_EX, INST_ID,
       INST_ID_HAZARD, INST_MEM, INST_WB, MEMORY_DATA_WB, multiplexer_1_out, multiplexer_3_out,
       multiplexer_4_out, multiplexer_5_out, multiplexer_6_out, NEXT_PC, NEXT_PC_WB, PC_EX, PC_ID, PC_MEM,
       rs1, rs1_EX, rs2, rs2_EX, WRITE_BACK;

  control_logic control_logic_1 (
    .CSRWen(CSRWen), .PCSel(PCSel), .RegWEn(RegWEn), .ImmSel(ImmSel), .BrUn(BrUn), .ASel(ASel), .BSel(BSel),
    .ALUSel(ALUSel), .MemRW(MemRW), .WBSel(WBSel), .CSRSel(CSRSel), .inst(INST_ID), .BrEq(BrEq), .BrLt(BrLt));
  Adder #(.width(32)) adder_1 (.a(PROGRAM_COUNTER), .b(32'h4), .out(adder_1_out));  // open: cin, cout
  Register #(.width(32)) PC (.D(multiplexer_1_out), .en(not_1_out), .clk(clk), .Q(PROGRAM_COUNTER));  // open: clr
  Multiplexer #(.enable("false"), .width(32)) multiplexer_1 (
    .in0(adder_1_out), .in1(ALU_RESULT), .out(multiplexer_1_out), .sel(PCSel_EX));
  not not_1 (not_1_out, HAZARD);
  not not_2 (not_2_out, HAZARD);
  not not_3 (not_3_out, HAZARD);
  Register #(.width(32)) register_1 (.D(PROGRAM_COUNTER), .en(not_2_out), .clk(clk), .Q(PC_ID));  // open: clr
  Register #(.width(32)) register_2 (.D(INSTRUCTION), .en(not_3_out), .clk(clk), .Q(INST_ID));  // open: clr
  Comparator #(.mode("unsigned"), .width(5)) comparator_1 (
    .a(INST_ID[19:15]), .b(rd_field_EX), .eq(comparator_1_eq));  // open: gt, lt
  Comparator #(.mode("unsigned"), .width(5)) comparator_2 (
    .a(INST_ID[24:20]), .b(rd_field_EX), .eq(comparator_2_eq));  // open: gt, lt
  Comparator #(.width(7)) comparator_3 (.a(INST_EX[6:0]), .b(7'b0000011), .eq(comparator_3_eq));  // open: gt, lt
  and and_1 (and_1_out, comparator_1_eq, not_4_out);
  not not_4 (not_4_out, ASel);
  and and_2 (and_2_out, comparator_2_eq, not_5_out);
  not not_5 (not_5_out, BSel);
  Multiplexer #(.enable("false"), .width(32)) multiplexer_2 (
    .in0(INST_ID), .in1(32'h33), .out(INST_ID_HAZARD), .sel(HAZARD));
  or or_1 (or_1_out, and_1_out, and_2_out);
  regfile regfile_1 (
    .rs1(INST_ID_HAZARD[19:15]), .rs2(INST_ID_HAZARD[24:20]), .rd(INST_ID_HAZARD[11:7]),
    .Write_Data(WRITE_BACK), .RegWEn(RegWEn_WB), .clk(clk), .ra(ra), .sp(sp), .t0(t0), .t1(t1), .t2(t2),
    .s0(s0), .s1(s1), .a0(a0), .Read_Data_1(rs1), .Read_Data_2(rs2));
  imm_gen imm_gen_1 (.inst(INST_ID_HAZARD), .ImmSel(ImmSel), .imm(imm));
  and and_3 (HAZARD, or_1_out, comparator_3_eq);
  Register #(.width(32)) register_3 (.D(PC_ID), .clk(clk), .Q(PC_EX));  // open: en, clr
  Register #(.width(32)) register_4 (.D(INST_ID), .clk(clk), .Q(INST_EX));  // open: en, clr
  Register #(.width(32)) register_5 (.D(rs1), .clk(clk), .Q(rs1_EX));  // open: en, clr
  Register #(.width(32)) register_6 (.D(rs2), .clk(clk), .Q(rs2_EX));  // open: en, clr
  Register #(.width(32)) register_7 (.D(imm), .clk(clk), .Q(imm_EX));  // open: en, clr
  Register #(.width(1)) register_8 (.D(PCSel), .clk(clk), .Q(PCSel_EX));  // open: en, clr
  Register #(.width(1)) register_9 (.D(RegWEn), .clk(clk), .Q(RegWEn_EX));  // open: en, clr
  Register #(.width(1)) register_10 (.D(BrUn), .clk(clk), .Q(BrUn_EX));  // open: en, clr
  Register #(.width(1)) register_11 (.D(ASel), .clk(clk), .Q(ASel_EX));  // open: en, clr
  Register #(.width(1)) register_12 (.D(BSel), .clk(clk), .Q(BSel_EX));  // open: en, clr
  Register #(.width(4)) register_13 (.D(ALUSel), .clk(clk), .Q(ALUSel_EX));  // open: en, clr
  Register #(.width(1)) register_14 (.D(MemRW), .clk(clk), .Q(MemRW_EX));  // open: en, clr
  Register #(.width(2)) register_15 (.D(WBSel), .clk(clk), .Q(WBSel_EX));  // open: en, clr
  Register #(.width(1)) register_16 (.D(CSRSel), .clk(clk), .Q(CSRSel_EX));  // open: en, clr
  Register #(.width(1)) register_17 (.D(CSRWen), .clk(clk), .Q(CSRWen_EX));  // open: en, clr
  Register #(.width(5)) register_18 (.D(INST_ID[19:15]), .clk(clk), .Q(rs1_field_EX));  // open: en, clr
  Register #(.width(5)) register_19 (.D(INST_ID[24:20]), .clk(clk), .Q(rs2_field_EX));  // open: en, clr
  Register #(.width(5)) register_20 (.D(INST_ID[11:7]), .clk(clk), .Q(rd_field_EX));  // open: en, clr
  Multiplexer #(.enable("false"), .select(2), .width(32)) multiplexer_3 (
    .in0(rs1_EX), .in1(WRITE_ADDRESS), .in2(MEMORY_DATA_WB), .out(multiplexer_3_out), .sel(FowardingA));  // open: in3
  Multiplexer #(.enable("false"), .select(2), .width(32)) multiplexer_4 (
    .in0(rs2_EX), .in1(WRITE_ADDRESS), .in2(MEMORY_DATA_WB), .out(multiplexer_4_out), .sel(FowardingB));  // open: in3
  Bit_Extender #(.in_width(32), .out_width(12)) bit_extender_1 (.in(imm_EX), .out(bit_extender_1_out));
  Comparator #(.mode("unsigned"), .width(5)) comparator_4 (
    .a(rs1_field_EX), .b(rd_field_MEM), .eq(FowardingA[0]));  // open: gt, lt
  Comparator #(.mode("unsigned"), .width(5)) comparator_5 (
    .a(rs2_field_EX), .b(rd_field_MEM), .eq(FowardingB[0]));  // open: gt, lt
  Comparator #(.mode("unsigned"), .width(5)) comparator_6 (
    .a(rs1_field_EX), .b(rd_field_WB), .eq(comparator_6_eq));  // open: gt, lt
  Comparator #(.mode("unsigned"), .width(5)) comparator_7 (
    .a(rs1_field_EX), .b(rd_field_MEM), .eq(comparator_7_eq));  // open: gt, lt
  Comparator #(.mode("unsigned"), .width(5)) comparator_8 (
    .a(rs2_field_EX), .b(rd_field_WB), .eq(comparator_8_eq));  // open: gt, lt
  Comparator #(.mode("unsigned"), .width(5)) comparator_9 (
    .a(rs2_field_EX), .b(rd_field_MEM), .eq(comparator_9_eq));  // open: gt, lt
  Multiplexer #(.enable("false"), .width(32)) multiplexer_5 (
    .in0(multiplexer_3_out), .in1(PC_EX), .out(multiplexer_5_out), .sel(ASel_EX));
  Multiplexer #(.enable("false"), .width(32)) multiplexer_6 (
    .in0(multiplexer_4_out), .in1(imm_EX), .out(multiplexer_6_out), .sel(BSel_EX));
  assign csr_uimm = {{27{1'b0}}, INST_EX[19:15]};  // Bit_Extender bit_extender_2
  Multiplexer #(.enable("false"), .width(32)) multiplexer_7 (
    .in0(rs1_EX), .in1(csr_uimm), .out(CSR_DATA), .sel(CSRSel_EX));
  not not_6 (not_6_out, comparator_7_eq);
  not not_7 (not_7_out, comparator_9_eq);
  alu alu_1 (.Result(ALU_RESULT), .A(multiplexer_5_out), .B(multiplexer_6_out), .ALUSel(ALUSel_EX));
  branch_comp branch_comp_1 (.rs1(rs1_EX), .rs2(rs2_EX), .BrUn(BrUn_EX), .BrEq(BrEq), .BrLt(BrLt));
  csr csr_1 (.CSR_address(bit_extender_1_out), .CSR_din(CSR_DATA), .CSR_WE(CSRWen_EX), .clk(clk), .tohost(tohost));
  and and_4 (FowardingA[1], comparator_6_eq, not_6_out);
  and and_5 (FowardingB[1], comparator_8_eq, not_7_out);
  Register #(.width(32)) register_21 (.D(PC_EX), .clk(clk), .Q(PC_MEM));  // open: en, clr
  Register #(.width(32)) register_22 (.D(INST_EX), .clk(clk), .Q(INST_MEM));  // open: en, clr
  Register #(.width(32)) register_23 (.D(ALU_RESULT), .clk(clk), .Q(WRITE_ADDRESS));  // open: en, clr
  Register #(.width(32)) register_24 (.D(rs2_EX), .clk(clk), .Q(WRITE_DATA));  // open: en, clr
  Register #(.width(1)) register_25 (.D(RegWEn_EX), .clk(clk), .Q(RegWEn_MEM));  // open: en, clr
  Register #(.width(1)) register_26 (.D(MemRW_EX), .clk(clk), .Q(MemRW_MEM));  // open: en, clr
  Register #(.width(2)) register_27 (.D(WBSel_EX), .clk(clk), .Q(WBSel_MEM));  // open: en, clr
  Register #(.width(5)) register_28 (.D(rd_field_EX), .clk(clk), .Q(rd_field_MEM));  // open: en, clr
  assign WRITE_ENABLE = {{3{MemRW_MEM}}, MemRW_MEM};  // Bit_Extender bit_extender_3
  Adder #(.width(32)) adder_2 (.a(PC_MEM), .b(32'h4), .out(NEXT_PC));  // open: cin, cout
  Register #(.width(32)) register_29 (.D(NEXT_PC), .clk(clk), .Q(NEXT_PC_WB));  // open: en, clr
  Register #(.width(32)) register_30 (.D(INST_MEM), .clk(clk), .Q(INST_WB));  // open: en, clr
  Register #(.width(32)) register_31 (.D(WRITE_ADDRESS), .clk(clk), .Q(ALU_RESULT_WB));  // open: en, clr
  Register #(.width(32)) register_32 (.D(READ_DATA), .clk(clk), .Q(MEMORY_DATA_WB));  // open: en, clr
  Register #(.width(1)) register_33 (.D(RegWEn_MEM), .clk(clk), .Q(RegWEn_WB));  // open: en, clr
  Register #(.width(2)) register_34 (.D(WBSel_MEM), .clk(clk), .Q(WBSel_WB));  // open: en, clr
  Register #(.width(5)) register_35 (.D(rd_field_MEM), .clk(clk), .Q(rd_field_WB));  // open: en, clr
  Multiplexer #(.enable("false"), .select(2), .width(32)) multiplexer_8 (
    .in0(NEXT_PC_WB), .in1(ALU_RESULT_WB), .in2(MEMORY_DATA_WB), .out(WRITE_BACK), .sel(WBSel_WB));  // open: in3

  // Other names for the same wires on the sheet: ALU_RESULT_MEM[31:0] = WRITE_ADDRESS;
  //   FowardingA_bit0 = FowardingA[0]; FowardingA_bit1 = FowardingA[1]; FowardingB_bit0 = FowardingB[0];
  //   FowardingB_bit1 = FowardingB[1]; rd_field[4:0] = INST_ID[11:7]; rs1_field[4:0] = INST_ID[19:15];
  //   rs2_field[4:0] = INST_ID[24:20]; rs2_MEM[31:0] = WRITE_DATA

  // Notes on the sheet:
  //   Output to IMEM
  //   IMEM (do **NOT** move this)
  //   Inputs from IMEM
  //   It is OK to move the PC, RegFile, ALU, MEM, Branch Comp, Imm Gen, and Control Logic to wherever is most convenient for you when constructing your CPU, and to delete this text
  //   Branch Control Hazard Unit in cpu.circ and some related part in control_logic.circ has not been finished.
  //   Inputs/Outputs for testing. Do **NOT** move these.
  //   Outputs To DMEM
  //   DMEM (do **NOT** move this)
  //   Inputs From DMEM
endmodule
